# Fritzing sketch 3.sensor.schematic (saved by Fritzing 0.9.3b)
breadboards: 1

parts:
  Part1 = Arduino Uno (Rev3)
  R1 = TRIMPOT [package=3386u]  # not connected
  R2 = TRIMPOT [package=3362u-2]
  R3 = TRIMPOT [package=3362u-2]
  R4 = Photocell (LDR) [package=THT]
  R5 = Resistor [tolerance=±5% resistance=220 package="0805 [SMD]"]

nets:
  N1: Part1.A0, R3.WIPER
  N2: Part1.A1, R2.WIPER
  N3: Part1.A2, R4.pin_0, R5.Pin_1
  N4: Part1.GND, R2.CCW, R3.CCW, R5.Pin_0
  N5: Part1.5V, R2.CW, R3.CW, R4.pin_1
